// Logisim project Conway-no_autoset.circ as structural Verilog: 1 circuit, main circuit main
module main (
  input  NE2,
  input  E3,
  input  Clock,
  input  Row,
  input  Column,
  input  Lock
);

  wire and_1_out, and_2_out, and_3_out, and_4_out, and_5_out, and_6_out, and_7_out, Btn_Invert_out, D_In_q,
       D_Out_q, not_1_out, not_2_out, not_3_out, or_1_out, or_2_out, or_3_out, or_4_out;

  Button Btn_Invert (.out(Btn_Invert_out));
  not not_1 (not_1_out, Clock);
  and and_1 (and_1_out, not_1_out, NE2);
  not not_2 (not_2_out, Lock);
  and and_2 (and_2_out, D_Out_q, not_2_out);
  and and_3 (and_3_out, E3, Lock);
  or or_1 (or_1_out, and_1_out, not_2_out);
  or or_2 (or_2_out, Clock, and_4_out);
  and and_4 (and_4_out, not_2_out, Btn_Invert_out);
  or or_3 (or_3_out, and_2_out, and_3_out);
  D_Flip_Flop D_In (.D(or_3_out), .clk(or_1_out), .Q(D_In_q));  // open: Qn, preset, reset
  not not_3 (not_3_out, D_Out_q);
  and and_5 (and_5_out, not_3_out, Btn_Invert_out);
  or or_4 (or_4_out, and_7_out, and_6_out);
  and and_6 (and_6_out, D_In_q, not_2_out);
  and and_7 (and_7_out, and_5_out, not_2_out);
  D_Flip_Flop D_Out (.D(or_4_out), .clk(or_2_out), .Q(D_Out_q));  // open: Qn, preset, reset
  LED led_1 (.in(D_Out_q));
endmodule
