// Logisim project Conway.circ as structural Verilog: 4 circuits, main circuit conway_cell
module conway_cell (
  input  Set_D_In,
  input  Row,
  input  Column,
  input  Lock,
  input  NN,
  input  NE,
  input  EE,
  input  ES,
  input  SS,
  input  SW,
  input  WW,
  input  NW,
  output Read_D_Out,
  output State_Out
);

  wire adder_1_cout, adder_1_out, adder_2_cout, adder_2_out, adder_3_cout, adder_3_out, adder_4_cout,
       adder_4_out, adder_5_cout, adder_5_out, adder_6_cout, adder_6_out, adder_7_cout, adder_7_out,
       adder_8_cout, adder_8_out, adder_9_cout, adder_9_out, adder_10_cout, adder_10_out, adder_11_cout,
       adder_11_out, Btn_Invert_out, eq_1_e3, eq_1_ne2;

  Button Btn_Invert (.out(Btn_Invert_out));
  Adder #(.width(1)) adder_1 (.a(NN), .b(NE), .out(adder_1_out), .cout(adder_1_cout));  // open: cin
  Adder #(.width(1)) adder_2 (.a(EE), .b(ES), .out(adder_2_out), .cout(adder_2_cout));  // open: cin
  Adder #(.width(1)) adder_3 (.a(SS), .b(SW), .out(adder_3_out), .cout(adder_3_cout));  // open: cin
  Adder #(.width(1)) adder_4 (.a(WW), .b(NW), .out(adder_4_out), .cout(adder_4_cout));  // open: cin
  Adder #(.width(1)) adder_5 (.a(adder_1_out), .b(adder_2_out), .out(adder_5_out), .cout(adder_5_cout));  // open: cin
  Adder #(.width(1)) adder_6 (
    .a(adder_1_cout), .b(adder_2_cout), .out(adder_6_out), .cin(adder_5_cout), .cout(adder_6_cout));
  Adder #(.width(1)) adder_7 (.a(adder_3_out), .b(adder_4_out), .out(adder_7_out), .cout(adder_7_cout));  // open: cin
  Adder #(.width(1)) adder_8 (
    .a(adder_3_cout), .b(adder_4_cout), .out(adder_8_out), .cin(adder_7_cout), .cout(adder_8_cout));
  Adder #(.width(1)) adder_9 (.a(adder_5_out), .b(adder_7_out), .out(adder_9_out), .cout(adder_9_cout));  // open: cin
  Adder #(.width(1)) adder_10 (
    .a(adder_6_out), .b(adder_8_out), .out(adder_10_out), .cin(adder_9_cout), .cout(adder_10_cout));
  Adder #(.width(1)) adder_11 (
    .a(adder_6_cout), .b(adder_8_cout), .out(adder_11_out), .cin(adder_10_cout), .cout(adder_11_cout));
  inner_logic inner_logic_1 (
    .Set_D_In(Set_D_In), .Row(Row), .Column(Column), .NE2(eq_1_ne2), .E3(eq_1_e3), .Btn(Lock),
    .Lock(Btn_Invert_out), .Read_D_Out(Read_D_Out), .State_Out(State_Out));
  LED led_1 (.in(State_Out));
  eq eq_1 (
    .A_LeastSig(adder_9_out), .B(adder_10_out), .C(adder_11_out), .D_MostSig(adder_11_cout), .NE2(eq_1_ne2),
    .E3(eq_1_e3));
endmodule

module inner_logic (
  input  Set_D_In,
  input  Row,
  input  Column,
  input  NE2,
  input  E3,
  input  Btn,
  input  Lock,
  output Read_D_Out,
  output State_Out
);

  wire and_1_out, and_2_out, and_3_out, and_4_out, and_5_out, and_6_out, and_7_out, and_8_out, and_9_out,
       and_10_out, and_11_out, and_12_out, and_14_out, clock_1_out, D_In_q, D_Out_qn, not_1_out, not_2_out,
       not_3_out, not_4_out, or_1_out, or_2_out, or_3_out, or_4_out, or_5_out, or_6_out;

  Clock clock_1 (.out(clock_1_out));
  not not_1 (not_1_out, clock_1_out);
  not not_2 (not_2_out, Lock);
  and and_1 (and_1_out, Row, Column);
  and and_2 (and_2_out, NE2, not_1_out);
  not not_3 (not_3_out, Btn);
  and and_3 (and_3_out, and_1_out, clock_1_out);
  and and_4 (and_4_out, and_2_out, Lock);
  and and_5 (and_5_out, not_2_out, Btn);
  and and_6 (and_6_out, not_3_out, not_2_out);
  and and_7 (and_7_out, D_Out_qn, not_2_out);
  and and_8 (and_8_out, E3, Lock);
  or or_1 (or_1_out, and_4_out, and_5_out);
  and and_9 (and_9_out, Set_D_In, and_1_out);
  not not_4 (not_4_out, and_1_out);
  or or_2 (or_2_out, and_7_out, and_8_out);
  or or_3 (or_3_out, and_3_out, or_1_out);
  and and_10 (and_10_out, clock_1_out, Lock);
  or or_4 (or_4_out, and_9_out, and_11_out);
  and and_11 (and_11_out, not_4_out, or_2_out);
  and and_12 (and_12_out, and_1_out, not_1_out);
  and and_13 (Read_D_Out, and_1_out, State_Out);
  or or_5 (or_5_out, and_10_out, and_6_out);
  and and_14 (and_14_out, not_4_out, or_5_out);
  D_Flip_Flop D_In (.D(or_4_out), .clk(or_3_out), .Q(D_In_q));  // open: Qn, preset, reset
  or or_6 (or_6_out, and_14_out, and_12_out);
  D_Flip_Flop D_Out (.D(D_In_q), .clk(or_6_out), .Q(State_Out), .Qn(D_Out_qn));  // open: preset, reset
endmodule

module eq (
  input  A_LeastSig,
  input  B,
  input  C,
  input  D_MostSig,
  output NE2,
  output E3
);

  wire and_1_out, and_2_out, nor_1_out, not_1_out;

  nor nor_1 (nor_1_out, C, D_MostSig);
  not not_1 (not_1_out, A_LeastSig);
  and and_1 (and_1_out, not_1_out, B);
  and and_2 (and_2_out, A_LeastSig, B);
  nand nand_1 (NE2, and_1_out, nor_1_out);
  and and_3 (E3, and_2_out, nor_1_out);
endmodule

module board_test (
);

  wire Column_sw1, Column_sw2, Column_sw3, conway_cell_1_state_out, conway_cell_2_read_d_out,
       conway_cell_2_state_out, conway_cell_3_state_out, conway_cell_4_state_out, conway_cell_5_state_out,
       conway_cell_6_state_out, conway_cell_7_state_out, conway_cell_8_state_out, conway_cell_9_state_out,
       conway_cell_10_state_out, D_In_sw1, Lock_sw1, Row_sw1, Row_sw2, Row_sw3, undriven, undriven_2,
       undriven_3, undriven_4, undriven_5, undriven_6, undriven_7, undriven_8, undriven_9, undriven_10,
       undriven_11, undriven_12, undriven_13, undriven_14, undriven_15, undriven_16, undriven_17,
       undriven_18, undriven_19, undriven_20, undriven_21, undriven_22, undriven_23, undriven_24,
       undriven_25, undriven_26, undriven_27, undriven_28, undriven_29, undriven_30, undriven_31,
       undriven_32, undriven_33, undriven_34, undriven_35, undriven_36;

  conway_cell conway_cell_1 (
    .Set_D_In(undriven_4), .Row(undriven_3), .Column(undriven_2), .Lock(undriven),
    .State_Out(conway_cell_1_state_out));  // open: NN, NE, EE, ES, SS, SW, WW, NW, Read_D_Out
  LED led_1 (.in(conway_cell_1_state_out));
  conway_cell conway_cell_2 (
    .Set_D_In(D_In_sw1), .Row(Row_sw3), .Column(Column_sw1), .Lock(Lock_sw1), .NN(undriven_5),
    .NE(undriven_6), .EE(conway_cell_5_state_out), .ES(conway_cell_6_state_out),
    .SS(conway_cell_3_state_out), .SW(undriven_7), .WW(undriven_8), .NW(undriven_9),
    .Read_D_Out(conway_cell_2_read_d_out), .State_Out(conway_cell_2_state_out));
  conway_cell conway_cell_3 (
    .Set_D_In(D_In_sw1), .Row(Row_sw2), .Column(Column_sw1), .Lock(Lock_sw1), .NN(conway_cell_2_state_out),
    .NE(conway_cell_5_state_out), .EE(conway_cell_6_state_out), .ES(conway_cell_7_state_out),
    .SS(conway_cell_4_state_out), .SW(undriven_10), .WW(undriven_11), .NW(undriven_12),
    .Read_D_Out(conway_cell_2_read_d_out), .State_Out(conway_cell_3_state_out));
  conway_cell conway_cell_4 (
    .Set_D_In(D_In_sw1), .Row(Row_sw1), .Column(Column_sw1), .Lock(Lock_sw1), .NN(conway_cell_3_state_out),
    .NE(conway_cell_6_state_out), .EE(conway_cell_7_state_out), .ES(undriven_13), .SS(undriven_14),
    .SW(undriven_15), .WW(undriven_16), .NW(undriven_17), .Read_D_Out(conway_cell_2_read_d_out),
    .State_Out(conway_cell_4_state_out));
  LED led_2 (.in(conway_cell_2_state_out));
  LED led_3 (.in(conway_cell_3_state_out));
  LED led_4 (.in(conway_cell_4_state_out));
  DipSwitch #(.number(3)) Row (.sw1(Row_sw1), .sw2(Row_sw2), .sw3(Row_sw3));
  DipSwitch #(.number(3)) Column (.sw1(Column_sw1), .sw2(Column_sw2), .sw3(Column_sw3));
  DipSwitch #(.number(1)) Lock (.sw1(Lock_sw1));
  DipSwitch #(.number(1)) D_In (.sw1(D_In_sw1));
  conway_cell conway_cell_5 (
    .Set_D_In(D_In_sw1), .Row(Row_sw3), .Column(Column_sw2), .Lock(Lock_sw1), .NN(undriven_19),
    .NE(undriven_18), .EE(conway_cell_8_state_out), .ES(conway_cell_9_state_out),
    .SS(conway_cell_6_state_out), .SW(conway_cell_3_state_out), .WW(conway_cell_2_state_out),
    .NW(undriven_20), .Read_D_Out(conway_cell_2_read_d_out), .State_Out(conway_cell_5_state_out));
  conway_cell conway_cell_6 (
    .Set_D_In(D_In_sw1), .Row(Row_sw2), .Column(Column_sw2), .Lock(Lock_sw1), .NN(conway_cell_5_state_out),
    .NE(conway_cell_8_state_out), .EE(conway_cell_9_state_out), .ES(conway_cell_10_state_out),
    .SS(conway_cell_7_state_out), .SW(conway_cell_4_state_out), .WW(conway_cell_3_state_out),
    .NW(conway_cell_2_state_out), .Read_D_Out(conway_cell_2_read_d_out), .State_Out(conway_cell_6_state_out));
  conway_cell conway_cell_7 (
    .Set_D_In(D_In_sw1), .Row(Row_sw1), .Column(Column_sw2), .Lock(Lock_sw1), .NN(conway_cell_6_state_out),
    .NE(conway_cell_9_state_out), .EE(conway_cell_10_state_out), .ES(undriven_21), .SS(undriven_22),
    .SW(undriven_23), .WW(conway_cell_4_state_out), .NW(conway_cell_3_state_out),
    .Read_D_Out(conway_cell_2_read_d_out), .State_Out(conway_cell_7_state_out));
  LED led_5 (.in(conway_cell_2_read_d_out));
  LED led_6 (.in(conway_cell_5_state_out));
  LED led_7 (.in(conway_cell_6_state_out));
  LED led_8 (.in(conway_cell_7_state_out));
  conway_cell conway_cell_8 (
    .Set_D_In(D_In_sw1), .Row(Row_sw3), .Column(Column_sw3), .Lock(Lock_sw1), .NN(undriven_36),
    .NE(undriven_24), .EE(undriven_25), .ES(undriven_26), .SS(conway_cell_9_state_out),
    .SW(conway_cell_6_state_out), .WW(conway_cell_5_state_out), .NW(undriven_27),
    .Read_D_Out(conway_cell_2_read_d_out), .State_Out(conway_cell_8_state_out));
  conway_cell conway_cell_9 (
    .Set_D_In(D_In_sw1), .Row(Row_sw2), .Column(Column_sw3), .Lock(Lock_sw1), .NN(conway_cell_8_state_out),
    .NE(undriven_28), .EE(undriven_29), .ES(undriven_30), .SS(conway_cell_10_state_out),
    .SW(conway_cell_7_state_out), .WW(conway_cell_6_state_out), .NW(conway_cell_5_state_out),
    .Read_D_Out(conway_cell_2_read_d_out), .State_Out(conway_cell_9_state_out));
  conway_cell conway_cell_10 (
    .Set_D_In(D_In_sw1), .Row(Row_sw1), .Column(Column_sw3), .Lock(Lock_sw1), .NN(conway_cell_9_state_out),
    .NE(undriven_31), .EE(undriven_32), .ES(undriven_33), .SS(undriven_34), .SW(undriven_35),
    .WW(conway_cell_7_state_out), .NW(conway_cell_6_state_out), .Read_D_Out(conway_cell_2_read_d_out),
    .State_Out(conway_cell_10_state_out));
  LED led_9 (.in(conway_cell_8_state_out));
  LED led_10 (.in(conway_cell_9_state_out));
  LED led_11 (.in(conway_cell_10_state_out));
endmodule
